// Logisim project cpu.circ as structural Verilog: 1 circuit, main circuit cpu
module cpu (
  input  clk,
  input  [31:0] INSTRUCTION,
  input  [31:0] READ_DATA,
  output [31:0] WRITE_ADDRESS,
  output [31:0] PROGRAM_COUNTER,
  output [31:0] ra,
  output [31:0] sp,
  output [31:0] t0,
  output [31:0] t1,
  output [31:0] t2,
  output [31:0] s0,
  output [31:0] s1,
  output [31:0] a0,
  output [31:0] tohost,
  output [3:0] WRITE_ENABLE,
  output [31:0] WRITE_DATA
);

  wire ASel, BrEq, BrLt, BrUn, BSel, CSRSel, CSRWen, LB, LH, MemRW, PCSel, RegWen, SB, SH;
  wire [1:0] WBSel;
  wire [2:0] ImmSel;
  wire [3:0] ALUSel, multiplexer_7_out, multiplexer_8_out;
  wire [4:0] AddrA, AddrB, AddrD;
  wire [31:0] adder_1_out, adder_2_out, ALU_INA, ALU_INB, bit_extender_1_out, bit_extender_2_out, DataA,
       IF_PIPED, IMM, LOAD_DATA, multiplexer_1_out, multiplexer_2_out, multiplexer_6_out, multiplexer_10_out,
       PC_PIPED, WBVal;

  Adder #(.width(32)) adder_1 (.a(PROGRAM_COUNTER), .b(32'h4), .out(adder_1_out));  // open: cin, cout
  Multiplexer #(.enable("false"), .width(32)) multiplexer_1 (
    .in0(adder_1_out), .in1(WRITE_ADDRESS), .out(multiplexer_1_out), .sel(PCSel));
  Multiplexer #(.enable("false"), .width(32)) multiplexer_2 (
    .in0(INSTRUCTION), .in1(32'h13), .out(multiplexer_2_out), .sel(PCSel));
  Register #(.width(32)) PC (.D(multiplexer_1_out), .clk(clk), .Q(PROGRAM_COUNTER));  // open: en, clr
  Register #(.width(32)) IF_Reg (
    .D(multiplexer_2_out), .clk(clk),
    .Q({IF_PIPED[31:25], AddrB, AddrA, IF_PIPED[14:12], AddrD, IF_PIPED[6:0]}));  // open: en, clr
  Register #(.width(32)) IF_PC (.D(PROGRAM_COUNTER), .clk(clk), .Q(PC_PIPED));  // open: en, clr
  imm_gen imm_gen_1 (
    .inst({IF_PIPED[31:25], AddrB, AddrA, IF_PIPED[14:12], AddrD, IF_PIPED[6:0]}), .ImmSel(ImmSel), .imm(IMM));
  control_logic control_logic_1 (
    .CSRWen(CSRWen), .lb(LB), .lh(LH), .sb(SB), .sh(SH), .PCSel(PCSel), .RegWEn(RegWen), .ImmSel(ImmSel),
    .BrUn(BrUn), .ASel(ASel), .BSel(BSel), .ALUSel(ALUSel), .MemRW(MemRW), .WBSel(WBSel), .CSRSel(CSRSel),
    .inst({IF_PIPED[31:25], AddrB, AddrA, IF_PIPED[14:12], AddrD, IF_PIPED[6:0]}), .BrEq(BrEq), .BrLt(BrLt));
  Multiplexer #(.enable("false"), .width(32)) multiplexer_3 (.in0(WRITE_DATA), .in1(IMM), .out(ALU_INB), .sel(BSel));
  Adder #(.width(32)) adder_2 (.a(PC_PIPED), .b(32'h4), .out(adder_2_out));  // open: cin, cout
  Multiplexer #(.enable("false"), .width(32)) multiplexer_4 (.in0(DataA), .in1(PC_PIPED), .out(ALU_INA), .sel(ASel));
  Multiplexer #(.enable("false"), .select(2), .width(32)) multiplexer_5 (
    .in0(LOAD_DATA), .in1(WRITE_ADDRESS), .in2(adder_2_out), .in3(IMM), .out(WBVal), .sel(WBSel));
  regfile regfile_1 (
    .rs1(AddrA), .rs2(AddrB), .rd(AddrD), .Write_Data(WBVal), .RegWEn(RegWen), .clk(clk), .ra(ra), .sp(sp),
    .t0(t0), .t1(t1), .t2(t2), .s0(s0), .s1(s1), .a0(a0), .Read_Data_1(DataA), .Read_Data_2(WRITE_DATA));
  Multiplexer #(.enable("false"), .width(32)) multiplexer_6 (
    .in0(DataA), .in1(IMM), .out(multiplexer_6_out), .sel(CSRSel));
  alu alu_1 (.Result(WRITE_ADDRESS), .A(ALU_INA), .B(ALU_INB), .ALUSel(ALUSel));
  // csr csr_1: pin names not known; wires that end beside it: 12'h51e, multiplexer_6_out, CSRWen, clk, tohost
  branch_comp branch_comp_1 (.rs1(DataA), .rs2(WRITE_DATA), .BrUn(BrUn), .BrEq(BrEq), .BrLt(BrLt));
  Multiplexer #(.enable("false"), .width(4)) multiplexer_7 (
    .in0(4'b1111), .in1(4'b0011), .out(multiplexer_7_out), .sel(SH));
  Multiplexer #(.enable("false"), .width(4)) multiplexer_8 (
    .in0(multiplexer_7_out), .in1(4'b0001), .out(multiplexer_8_out), .sel(SB));
  assign bit_extender_1_out = {{24{READ_DATA[7]}}, READ_DATA[7:0]};  // Bit_Extender bit_extender_1
  assign bit_extender_2_out = {{16{READ_DATA[15]}}, READ_DATA[15:0]};  // Bit_Extender bit_extender_2
  Multiplexer #(.enable("false"), .width(4)) multiplexer_9 (
    .in0(4'b0000), .in1(multiplexer_8_out), .out(WRITE_ENABLE), .sel(MemRW));
  Multiplexer #(.enable("false"), .width(32)) multiplexer_10 (
    .in0(READ_DATA), .in1(bit_extender_2_out), .out(multiplexer_10_out), .sel(LH));
  Multiplexer #(.enable("false"), .width(32)) multiplexer_11 (
    .in0(multiplexer_10_out), .in1(bit_extender_1_out), .out(LOAD_DATA), .sel(LB));

  // Other names for the same wires on the sheet: ALU_OUT[31:0] = WRITE_ADDRESS; DataB[31:0] = WRITE_DATA;
  //   IF_PIPED (some bits) = {AddrB, AddrA, AddrD}

  // Notes on the sheet:
  //   Output to IMEM
  //   IMEM (do **NOT** move this)
  //   Inputs from IMEM
  //   It is OK to move the PC, RegFile, ALU, MEM, Branch Comp, Imm Gen, and Control Logic to wherever is most convenient for you when constructing your CPU, and to delete this text
  //   SH
  //   SB
  //   Inputs/Outputs for testing. Do **NOT** move these.
  //   Outputs To DMEM
  //   DMEM (do **NOT** move this)
  //   Inputs From DMEM
endmodule
