// Logisim project imm_gen.circ as structural Verilog: 1 circuit, main circuit imm_gen
module imm_gen (
  input  [31:0] inst,
  input  [2:0] ImmSel,
  output [31:0] imm
);

  wire [31:0] bit_extender_3_out, bit_extender_4_out, bit_extender_5_out, imm_b, imm_i, imm_j, imm_s, imm_u;

  assign imm_i = {{20{inst[31]}}, inst[31:20]};  // Bit_Extender bit_extender_1
  assign imm_s = {{20{inst[31]}}, {inst[31:25], inst[11:7]}};  // Bit_Extender bit_extender_2
  assign bit_extender_3_out = {{12{inst[31]}}, inst[31:12]};  // Bit_Extender bit_extender_3
  assign bit_extender_4_out = {{12{inst[31]}}, {inst[31], inst[19:12], inst[20], inst[30:21]}};  // Bit_Extender bit_extender_4
  Multiplexer #(.enable("false"), .select(3), .width(32)) multiplexer_1 (
    .in0(imm_i), .in1(imm_s), .in2(imm_b), .in3(imm_u), .in4(imm_j), .out(imm), .sel(ImmSel));  // open: in5, in6, in7
  assign bit_extender_5_out = {{20{inst[31]}}, {inst[31], inst[7], inst[30:25], inst[11:8]}};  // Bit_Extender bit_extender_5
  Shifter #(.width(32)) shifter_1 (.in(bit_extender_3_out), .\dist (5'b01100), .out(imm_u));
  Shifter #(.width(32)) shifter_2 (.in(bit_extender_4_out), .\dist (5'b00001), .out(imm_j));
  Shifter #(.width(32)) shifter_3 (.in(bit_extender_5_out), .\dist (5'b00001), .out(imm_b));

  // Notes on the sheet:
  //   INPUTS to your circuit
  //   DON'T CHANGE THE LOCATIONS OF THE INPUTS AND OUTPUTS!
  //   OUTPUT from your circuit
endmodule
